// Logisim project rippleAdderSubtractor.circ as structural Verilog: 1 circuit, main circuit main
module main (
  input  A3,
  input  A2,
  input  A1,
  input  A0,
  input  Subtract,
  input  B3,
  input  B2,
  input  B1,
  input  B0,
  output Cout,
  output S3,
  output S2,
  output S1,
  output S0,
  output S0_2,
  output S1_2,
  output S2_2,
  output S3_2,
  output Cout_2,
  output Cin,
  output C0,
  output C1,
  output C2
);

  wire and_1_out, and_2_out, and_3_out, and_4_out, and_5_out, and_6_out, and_7_out, and_8_out, xor_1_out,
       xor_2_out, xor_5_out, xor_6_out, xor_9_out, xor_10_out, xor_13_out, xor_14_out;

  xor xor_1 (xor_1_out, Subtract, B0);
  xor xor_2 (xor_2_out, A0, xor_1_out);
  and and_1 (and_1_out, A0, xor_1_out);
  xor xor_3 (S0, xor_2_out, Subtract);
  and and_2 (and_2_out, xor_2_out, Subtract);
  xor xor_4 (C0, and_2_out, and_1_out);
  xor xor_5 (xor_5_out, Subtract, B1);
  xor xor_6 (xor_6_out, A1, xor_5_out);
  and and_3 (and_3_out, A1, xor_5_out);
  xor xor_7 (S1, xor_6_out, C0);
  and and_4 (and_4_out, xor_6_out, C0);
  xor xor_8 (C1, and_4_out, and_3_out);
  xor xor_9 (xor_9_out, Subtract, B2);
  xor xor_10 (xor_10_out, A2, xor_9_out);
  and and_5 (and_5_out, A2, xor_9_out);
  xor xor_11 (S2, xor_10_out, C1);
  and and_6 (and_6_out, xor_10_out, C1);
  xor xor_12 (C2, and_6_out, and_5_out);
  xor xor_13 (xor_13_out, Subtract, B3);
  xor xor_14 (xor_14_out, A3, xor_13_out);
  and and_7 (and_7_out, A3, xor_13_out);
  xor xor_15 (S3, xor_14_out, C2);
  and and_8 (and_8_out, xor_14_out, C2);
  xor xor_16 (Cout, and_8_out, and_7_out);

  assign Cin = Subtract;
  assign Cout_2 = Cout;
  assign S0_2 = S0;
  assign S1_2 = S1;
  assign S2_2 = S2;
  assign S3_2 = S3;
endmodule
